# Fritzing sketch Arduino-diagram (saved by Fritzing 0.9.4)

parts:
  Arduino_Uno = Arduino Uno (Rev3)
  ws2812b_LED_Strip = WS2812 RGB LED strip
  5V_Power_Supply = generic-ac-power-supply [package=THT]
  KY-022_Infrared_Reciever = KY-022 Infrared Receiver Module [package="Breakout board"]
  R1 = Resistor [tolerance=±5% resistance=220 package=THT]

nets:
  N1: Arduino_Uno.D5_PWM, R1.Pin_0
  N2: Arduino_Uno.D7, KY-022_Infrared_Reciever.S
  3V3: Arduino_Uno.3V3, KY-022_Infrared_Reciever.Vin
  GND: Arduino_Uno.GND, ws2812b_LED_Strip.GND, 5V_Power_Supply.pin3#3, KY-022_Infrared_Reciever.-
  N3: ws2812b_LED_Strip.VCC, 5V_Power_Supply.pin3#2
  N4: ws2812b_LED_Strip.DIN, R1.Pin_1

custom parts:
  WS2812 RGB LED strip: WS2812 strip
  generic-ac-power-supply: Generic ac power supply module. Use as is, or customize the svgs to fit your particular device (as they are all different.) Provides AC input and single DC output. PCB is generic and will need modifications if you intend to do a pcb mount.
  KY-022 Infrared Receiver Module: KY-022 IR receiver module, reacts to 38kHz infrared light.
